# Fritzing sketch Prototype-Design (saved by Fritzing 0.9.3b)
breadboards: 1

parts:
  M1 = DOIT Esp32 DevKit v1 (30 pins long, 11 pins width) [part_number=ESP32S-PIN30]
  Keypad4x1 = Keypad Membran 4x4
  J1 = Piezo Speaker
  LED1 = LED - 5mm [color="Red (633nm)" package="5 mm [THT]"]
  LED2 = LED - 5mm [color="Green (555nm)" package="5 mm [THT]"]
  R1 = Resistor [tolerance=±5% resistance=220 package=THT]
  R2 = Resistor [tolerance=±5% resistance=220 package=THT]
  Part1 = RFID-RC522-v2

nets:
  3V3: M1.3V3, Part1.3.3V
  GND: M1.GND, J1.pin1, LED1.cathode, LED2.cathode, Part1.GND
  N1: M1.D15, J1.pin2
  N2: M1.D5, Part1.SDA
  N3: M1.D18, Part1.SCK
  N4: M1.D19, Part1.MISO
  N5: M1.D22, Part1.RST
  N6: M1.D23, Part1.MOSI
  N7: M1.D34, Keypad4x1.Pin8
  N8: M1.D35, Keypad4x1.Pin7
  N9: M1.D32, Keypad4x1.Pin6
  N10: M1.D33, Keypad4x1.Pin5
  N11: M1.D25, Keypad4x1.Pin4
  N12: M1.D26, Keypad4x1.Pin3
  N13: M1.D27, Keypad4x1.Pin2
  N14: M1.D14, Keypad4x1.Pin1
  N15: M1.D12, R1.Pin_0
  N16: M1.D13, R2.Pin_0
  N17: LED1.anode, R1.Pin_1
  N18: LED2.anode, R2.Pin_1

custom parts:
  DOIT Esp32 DevKit v1 (30 pins long, 11 pins width): The DOIT Esp32 DevKit v1 is one of the development board created by DOIT to evaluate the ESP-WROOM-32 module. It is based on the ESP32 microcontroller that boasts Wifi, Bluetooth, Ethernet and Low Power support all in a single chip. (vanepp) made breadboard work, adjusted pin numbering and labels and reduced size of schematic and cleaned up pcb. This chip is 30pins long (2 x15) and 11 pins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
  Keypad Membran 4x4: Membrane Keypad 4x4 Matrix
  RFID-RC522-v2: A simple China made RFID-RC522 Reader; do check the pin labels, as this is a MFRC522 based clone.
